# Fritzing sketch Ice_Maker_Electrical_Drawing_fixed (1) (saved by Fritzing 0.9.3b)
breadboards: 1

parts:
  U1 = ESP32-38PinWide [part_number=ESP32-38PinWide]
  YF-S201_Flow_Meter1 = YF-S201 Water Flow Meter
  A1 = 2957N11 pressure sensor
  VALVE1 = Plastic Solenoid Valve
  A2 = 2-Channel 5v Relay Shield [package=relay-2ch5v10a]
  M1 = water level switch
  AMS1 = AMS1777 5V regulator module
  WATER_PUMP1 = water pump/motor
  D1 = P1000K [part_number=P1000K]
  VCC1 = Battery
  A3 = Hanmatek HM305

nets:
  N1: U1.3.3, YF-S201_Flow_Meter1.VCC
  N2: U1.EN, U1.GPIO36, A1.Pin_3
  N3: U1.GPIO26, U1.GPIO27, M1.pin1
  GND: U1.GND, U1.GPIO13, YF-S201_Flow_Meter1.GND, A2.Pin_10, A2.Pin_11
  N4: U1.GPIO11, U1.VIN, A1.Pin_1, A1.Pin_2, A2.Pin_13
  N5: U1.GPIO5, YF-S201_Flow_Meter1.SIG
  N6: U1.GPIO21, A2.Pin_12
  N7: VALVE1.no_name_yet#1, A2.Pin_2, D1.cathode
  N8: VALVE1.no_name_yet#2, AMS1.GND-_(output), D1.anode
  N9: A2.Pin_1, AMS1.VOUT+
  N10: A2.Pin_4, VCC1.+
  N11: A2.Pin_5, WATER_PUMP1.pin_2
  N12: AMS1.VIN+, A3.Pin_4
  N13: AMS1.GND-_(input), A3.Pin_3
  N14: WATER_PUMP1.pin_1, VCC1.-

custom parts:
  ESP32-38PinWide: Generic 38-Pin ESP32 with wide format (only access to one side of pins on a breadboard) based on Stephen Lilley's HiLetgo ESP-WROOM-32 ESP32 ESP-32S Development Board.
  YF-S201 Water Flow Meter: The YF-S201 Flow Meter. The input voltage is 5V to 24V (DC).
  2957N11 pressure sensor: Monitor and control vacuum pumps, air compressors, and hydraulics. These transmitters convert both pressure and vacuum into an electrical signal that can be interpreted by receiving devices, such as remote displays, programmable logic controllers, and motor speed controls.
  2-Channel 5v Relay Shield: 2 Channel 5v Relay Shield w. 2x SPD-06VDC-SD-C
  water level switch: Generic water level float switch.
  AMS1777 5V regulator module: AMS1777 5V regulator module source : https://github.com/ShenTengTu/fritzing_parts/tree/master/voltage%20regulator/AMS1117_5V_regulator_module
  water pump/motor: WATER PUMP BY ARDUBLOCKTR
  Hanmatek HM305: DC Power Supply 30V5A HM305.
