# Fritzing sketch Prototype Ice-Maker PCB (saved by Fritzing 0.9.3b)
circuit board: 12cm x 9cm
breadboards: 1

parts:
  U1 = ESP32-38PinWide [part_number=ESP32-38PinWide]
  A1 = 2-Channel 5v Relay Shield [package=relay-2ch5v10a]
  DHT1 = DHT11 Humitidy and Temperature Sensor (3 pins)
  YF-S201_Flow_Meter1 = YF-S201 Water Flow Meter
  A2 = 2957N11 pressure sensor
  A3 = 2957N11 pressure sensor
  M1 = water level switch
  AMS1 = AMS1777 5V regulator module
  VCC1 = Battery block 9V
  Part1 = Humidity Sensor - HIH-4030 Breakout

nets:
  N1: U1.3.3, DHT1.Plus, YF-S201_Flow_Meter1.VCC
  N2: U1.GPIO34, A3.Pin_3
  N3: U1.GPIO35, A2.Pin_3
  N4: U1.GPIO32, Part1.OUT
  N5: U1.GPIO26, DHT1.Signal
  N6: U1.GPIO27, M1.pin1
  GND: U1.GND, A1.Pin_10, DHT1.Gnd, YF-S201_Flow_Meter1.GND, A2.Pin_1, A3.Pin_1, M1.pin2, AMS1.GND-_(output), Part1.GND
  VIN: U1.VIN, A1.Pin_13, A2.Pin_2, A3.Pin_2, AMS1.VOUT+, Part1.VCC
  N7: U1.GPIO5, YF-S201_Flow_Meter1.SIG
  N8: U1.GPIO18, A1.Pin_12
  N9: U1.GPIO21, A1.Pin_11
  N10: AMS1.VIN+, VCC1.+
  N11: AMS1.GND-_(input), VCC1.-

custom parts:
  ESP32-38PinWide: Generic 38-Pin ESP32 with wide format (only access to one side of pins on a breadboard) based on Stephen Lilley's HiLetgo ESP-WROOM-32 ESP32 ESP-32S Development Board.
  2-Channel 5v Relay Shield: 2 Channel 5v Relay Shield w. 2x SPD-06VDC-SD-C
  DHT11 Humitidy and Temperature Sensor (3 pins): DHT11 Humidity and Temperature Sensor (3 pins).
  YF-S201 Water Flow Meter: The YF-S201 Flow Meter. The input voltage is 5V to 24V (DC).
  2957N11 pressure sensor: Monitor and control vacuum pumps, air compressors, and hydraulics. These transmitters convert both pressure and vacuum into an electrical signal that can be interpreted by receiving devices, such as remote displays, programmable logic controllers, and motor speed controls.
  water level switch: Generic water level float switch.
  AMS1777 5V regulator module: AMS1777 5V regulator module source : https://github.com/ShenTengTu/fritzing_parts/tree/master/voltage%20regulator/AMS1117_5V_regulator_module
